// Logisim project 32位ALU.circ as structural Verilog
module \_4位先行进位电路  (
  input  in_1,
  input  in_2,
  input  in_3,
  input  in_4,
  input  in_5,
  input  in_6,
  input  in_7,
  input  in_8,
  input  in_9,
  output out_10,
  output out_11,
  output out_12,
  output out_13,
  output out_14,
  output out_15
);

  wire and_2_out, and_3_out, and_4_out, and_5_out, and_6_out, and_7_out, and_8_out, and_9_out, and_10_out,
       and_11_out, and_12_out, and_13_out, and_14_out;

  and and_1 (out_15, in_2, in_4, in_6, in_8);
  or or_1 (out_14, in_1, and_3_out, and_2_out, and_4_out);
  and and_2 (and_2_out, in_4, in_2, in_5);
  and and_3 (and_3_out, in_2, in_3);
  and and_4 (and_4_out, in_7, in_6, in_4, in_2);
  and and_5 (and_5_out, in_2, in_3);
  and and_6 (and_6_out, in_2, in_4, in_5);
  or or_2 (out_10, in_1, and_5_out, and_6_out, and_7_out, and_8_out);
  and and_7 (and_7_out, in_2, in_4, in_6, in_7);
  and and_8 (and_8_out, in_2, in_4, in_6, in_8, in_9);
  and and_9 (and_9_out, in_4, in_5);
  or or_3 (out_11, in_3, and_9_out, and_11_out, and_10_out);
  and and_10 (and_10_out, in_4, in_6, in_8, in_9);
  and and_11 (and_11_out, in_4, in_6, in_7);
  or or_4 (out_12, in_5, and_12_out, and_14_out);
  and and_12 (and_12_out, in_6, in_7);
  or or_5 (out_13, in_7, and_13_out);
  and and_13 (and_13_out, in_8, in_9);
  and and_14 (and_14_out, in_6, in_8, in_9);

  // Other names for the same wires on the sheet: C0 = in_9; C1 = out_13; C2 = out_12; C3 = out_11; C4 = out_10;
  //   G1 = in_7; G2 = in_5; G3 = in_3; G4 = in_1; G_star = out_14; P1 = in_8; P2 = in_6; P3 = in_4; P4 = in_2;
  //   P_star = out_15

  // Notes on the sheet:
  //   输入引脚区
  //   数据计算部分
  //   输出引脚区
endmodule

module \_4位快速加法器  (
  input  in_1,
  input  [3:0] in_2,
  input  [3:0] in_3,
  output \输出引脚区 ,
  output out_5,
  output out_6,
  output out_7,
  output [3:0] out_8
);

  wire and_1_out, and_2_out, and_3_out, and_4_out, \n4位先行进位电路_1_out_12 , \n4位先行进位电路_1_out_13 , xor_3_out,
       xor_4_out, xor_5_out, xor_6_out;

  xor xor_1 (out_8[3], xor_3_out, out_5);
  xor xor_2 (out_8[2], xor_4_out, \n4位先行进位电路_1_out_12 );
  and and_1 (and_1_out, in_2[3], in_3[3]);
  xor xor_3 (xor_3_out, in_2[3], in_3[3]);
  and and_2 (and_2_out, in_2[2], in_3[2]);
  \_4位先行进位电路  \u_4位先行进位电路_1  (
    .in_1(and_1_out), .in_2(xor_3_out), .in_3(and_2_out), .in_4(xor_4_out), .in_5(and_3_out),
    .in_6(xor_5_out), .in_7(and_4_out), .in_8(xor_6_out), .in_9(in_1), .out_10(\输出引脚区 ), .out_11(out_5),
    .out_12(\n4位先行进位电路_1_out_12 ), .out_13(\n4位先行进位电路_1_out_13 ), .out_14(out_6), .out_15(out_7));
  xor xor_4 (xor_4_out, in_2[2], in_3[2]);
  and and_3 (and_3_out, in_2[1], in_3[1]);
  xor xor_5 (xor_5_out, in_2[1], in_3[1]);
  and and_4 (and_4_out, in_2[0], in_3[0]);
  xor xor_6 (xor_6_out, in_2[0], in_3[0]);
  xor xor_7 (out_8[0], xor_6_out, in_1);
  xor xor_8 (out_8[1], \n4位先行进位电路_1_out_13 , xor_5_out);

  // Other names for the same wires on the sheet: C0 = in_1; C3 = out_5; C4 = \输出引脚区 ; G_star = out_6; P_star = out_7;
  //   S[3:0] = out_8; s0 = out_8[0]; s1 = out_8[1]; s2 = out_8[2]; s3 = out_8[3]; X[3:0] = in_2; x0 = in_2[0];
  //   x1 = in_2[1]; x2 = in_2[2]; x3 = in_2[3]; Y[3:0] = in_3; y0 = in_3[0]; y1 = in_3[1]; y2 = in_3[2]; y3 = in_3[3]

  // Notes on the sheet:
  //   输入引脚区
  //   进位输入
  //   计算区
  //   进位位
endmodule

module \_16位快速加法器  (
  input  [15:0] in_1,
  input  [15:0] in_2,
  input  in_3,
  output [15:0] out_4,
  output out_5,
  output out_6,
  output out_7,
  output out_8
);

  wire \n4位先行进位电路_1_out_11 , \n4位先行进位电路_1_out_12 , \n4位先行进位电路_1_out_13 , \n4位快速加法器_1_out_6 ,
       \n4位快速加法器_1_out_7 , \n4位快速加法器_2_out_6 , \n4位快速加法器_2_out_7 , \n4位快速加法器_3_out_6 , \n4位快速加法器_3_out_7 ,
       \n4位快速加法器_4_out_6 , \n4位快速加法器_4_out_7 ;

  \_4位快速加法器  \u_4位快速加法器_1  (
    .in_2(in_1[15:12]), .in_3(in_2[15:12]), .out_8(out_4[15:12]), .in_1(\n4位先行进位电路_1_out_11 ),
    .\输出引脚区 (out_6), .out_6(\n4位快速加法器_1_out_6 ), .out_7(\n4位快速加法器_1_out_7 ));  // open: out_5
  \_4位先行进位电路  \u_4位先行进位电路_1  (
    .in_1(\n4位快速加法器_1_out_6 ), .in_2(\n4位快速加法器_1_out_7 ), .in_3(\n4位快速加法器_2_out_6 ),
    .in_4(\n4位快速加法器_2_out_7 ), .in_5(\n4位快速加法器_3_out_6 ), .in_6(\n4位快速加法器_3_out_7 ),
    .in_7(\n4位快速加法器_4_out_6 ), .in_8(\n4位快速加法器_4_out_7 ), .in_9(in_3), .out_10(out_5),
    .out_11(\n4位先行进位电路_1_out_11 ), .out_12(\n4位先行进位电路_1_out_12 ), .out_13(\n4位先行进位电路_1_out_13 ),
    .out_14(out_7), .out_15(out_8));
  \_4位快速加法器  \u_4位快速加法器_2  (
    .in_2(in_1[11:8]), .in_3(in_2[11:8]), .out_8(out_4[11:8]), .in_1(\n4位先行进位电路_1_out_12 ),
    .out_6(\n4位快速加法器_2_out_6 ), .out_7(\n4位快速加法器_2_out_7 ));  // open: 输出引脚区, out_5
  \_4位快速加法器  \u_4位快速加法器_3  (
    .in_2(in_1[7:4]), .in_3(in_2[7:4]), .out_8(out_4[7:4]), .in_1(\n4位先行进位电路_1_out_13 ),
    .out_6(\n4位快速加法器_3_out_6 ), .out_7(\n4位快速加法器_3_out_7 ));  // open: 输出引脚区, out_5
  // Probe on in_1
  // Probe on in_2
  // Probe on out_4
  // Probe on in_1
  // Probe on in_2
  // Probe on out_4
  \_4位快速加法器  \u_4位快速加法器_4  (
    .in_2(in_1[3:0]), .in_3(in_2[3:0]), .out_8(out_4[3:0]), .in_1(in_3), .out_6(\n4位快速加法器_4_out_6 ),
    .out_7(\n4位快速加法器_4_out_7 ));  // open: 输出引脚区, out_5

  // Other names for the same wires on the sheet: C0 = in_3; C15 = out_6; C16 = out_5; G_star = out_7; P_star = out_8;
  //   S[15:0] = out_4; s0[3:0] = out_4[3:0]; s1[3:0] = out_4[7:4]; s2[3:0] = out_4[11:8]; s3[3:0] = out_4[15:12];
  //   X[15:0] = in_1; x0[3:0] = in_1[3:0]; x1[3:0] = in_1[7:4]; x2[3:0] = in_1[11:8]; x3[3:0] = in_1[15:12];
  //   Y[15:0] = in_2; y0[3:0] = in_2[3:0]; y1[3:0] = in_2[7:4]; y2[3:0] = in_2[11:8]; y3[3:0] = in_2[15:12]

  // Notes on the sheet:
  //   输入引脚区
  //   输出引脚区
  //   计算部分
  //   有符号加法
  //   无符号加法
endmodule

module \_32位快速加法器  (
  input  [31:0] in_1,
  input  [31:0] in_2,
  input  in_3,
  output [31:0] out_4,
  output out_5,
  output out_6
);

  wire \n4位先行进位电路_1_out_11 , \n4位先行进位电路_1_out_12 , \n4位先行进位电路_1_out_13 , \n4位先行进位电路_2_out_10 ,
       \n4位先行进位电路_2_out_11 , \n4位先行进位电路_2_out_12 , \n4位先行进位电路_2_out_13 , \n4位快速加法器_1_out_6 ,
       \n4位快速加法器_1_out_7 , \n4位快速加法器_2_out_6 , \n4位快速加法器_2_out_7 , \n4位快速加法器_3_out_6 , \n4位快速加法器_3_out_7 ,
       \n4位快速加法器_4_out_6 , \n4位快速加法器_4_out_7 , \n4位快速加法器_5_out_6 , \n4位快速加法器_5_out_7 , \n4位快速加法器_6_out_6 ,
       \n4位快速加法器_6_out_7 , \n4位快速加法器_7_out_6 , \n4位快速加法器_7_out_7 , \n4位快速加法器_8_out_6 , \n4位快速加法器_8_out_7 ;

  \_4位快速加法器  \u_4位快速加法器_1  (
    .in_2(in_1[31:28]), .in_3(in_2[31:28]), .out_8(out_4[31:28]), .in_1(\n4位先行进位电路_1_out_11 ),
    .\输出引脚区 (out_6), .out_5(out_5), .out_6(\n4位快速加法器_1_out_6 ), .out_7(\n4位快速加法器_1_out_7 ));
  \_4位快速加法器  \u_4位快速加法器_2  (
    .in_2(in_1[27:24]), .in_3(in_2[27:24]), .out_8(out_4[27:24]), .in_1(\n4位先行进位电路_1_out_12 ),
    .out_6(\n4位快速加法器_2_out_6 ), .out_7(\n4位快速加法器_2_out_7 ));  // open: 输出引脚区, out_5
  \_4位先行进位电路  \u_4位先行进位电路_1  (
    .in_1(\n4位快速加法器_1_out_6 ), .in_2(\n4位快速加法器_1_out_7 ), .in_3(\n4位快速加法器_2_out_6 ),
    .in_4(\n4位快速加法器_2_out_7 ), .in_5(\n4位快速加法器_3_out_6 ), .in_6(\n4位快速加法器_3_out_7 ),
    .in_7(\n4位快速加法器_4_out_6 ), .in_8(\n4位快速加法器_4_out_7 ), .in_9(\n4位先行进位电路_2_out_10 ),
    .out_11(\n4位先行进位电路_1_out_11 ), .out_12(\n4位先行进位电路_1_out_12 ), .out_13(\n4位先行进位电路_1_out_13 ));  // open: out_10, out_14, out_15
  \_4位快速加法器  \u_4位快速加法器_3  (
    .in_2(in_1[23:20]), .in_3(in_2[23:20]), .out_8(out_4[23:20]), .in_1(\n4位先行进位电路_1_out_13 ),
    .out_6(\n4位快速加法器_3_out_6 ), .out_7(\n4位快速加法器_3_out_7 ));  // open: 输出引脚区, out_5
  \_4位快速加法器  \u_4位快速加法器_4  (
    .in_2(in_1[19:16]), .in_3(in_2[19:16]), .out_8(out_4[19:16]), .in_1(\n4位先行进位电路_2_out_10 ),
    .out_6(\n4位快速加法器_4_out_6 ), .out_7(\n4位快速加法器_4_out_7 ));  // open: 输出引脚区, out_5
  \_4位快速加法器  \u_4位快速加法器_5  (
    .in_2(in_1[15:12]), .in_3(in_2[15:12]), .out_8(out_4[15:12]), .in_1(\n4位先行进位电路_2_out_11 ),
    .out_6(\n4位快速加法器_5_out_6 ), .out_7(\n4位快速加法器_5_out_7 ));  // open: 输出引脚区, out_5
  \_4位快速加法器  \u_4位快速加法器_6  (
    .in_2(in_1[11:8]), .in_3(in_2[11:8]), .out_8(out_4[11:8]), .in_1(\n4位先行进位电路_2_out_12 ),
    .out_6(\n4位快速加法器_6_out_6 ), .out_7(\n4位快速加法器_6_out_7 ));  // open: 输出引脚区, out_5
  // Probe on in_1
  // Probe on in_2
  // Probe on out_4
  // Probe on in_1
  // Probe on in_2
  // Probe on out_4
  \_4位先行进位电路  \u_4位先行进位电路_2  (
    .in_1(\n4位快速加法器_5_out_6 ), .in_2(\n4位快速加法器_5_out_7 ), .in_3(\n4位快速加法器_6_out_6 ),
    .in_4(\n4位快速加法器_6_out_7 ), .in_5(\n4位快速加法器_7_out_6 ), .in_6(\n4位快速加法器_7_out_7 ),
    .in_7(\n4位快速加法器_8_out_6 ), .in_8(\n4位快速加法器_8_out_7 ), .in_9(in_3), .out_10(\n4位先行进位电路_2_out_10 ),
    .out_11(\n4位先行进位电路_2_out_11 ), .out_12(\n4位先行进位电路_2_out_12 ), .out_13(\n4位先行进位电路_2_out_13 ));  // open: out_14, out_15
  \_4位快速加法器  \u_4位快速加法器_7  (
    .in_2(in_1[7:4]), .in_3(in_2[7:4]), .out_8(out_4[7:4]), .in_1(\n4位先行进位电路_2_out_13 ),
    .out_6(\n4位快速加法器_7_out_6 ), .out_7(\n4位快速加法器_7_out_7 ));  // open: 输出引脚区, out_5
  \_4位快速加法器  \u_4位快速加法器_8  (
    .in_2(in_1[3:0]), .in_3(in_2[3:0]), .out_8(out_4[3:0]), .in_1(in_3), .out_6(\n4位快速加法器_8_out_6 ),
    .out_7(\n4位快速加法器_8_out_7 ));  // open: 输出引脚区, out_5

  // Other names for the same wires on the sheet: C0 = in_3; C31 = out_6; C32 = out_5; S[31:0] = out_4;
  //   s0[3:0] = out_4[3:0]; s1[3:0] = out_4[7:4]; s2[3:0] = out_4[11:8]; s3[3:0] = out_4[15:12];
  //   s4[3:0] = out_4[19:16]; s5[3:0] = out_4[23:20]; s6[3:0] = out_4[27:24]; s7[3:0] = out_4[31:28]; X[31:0] = in_1;
  //   x0[3:0] = in_1[3:0]; x1[3:0] = in_1[7:4]; x2[3:0] = in_1[11:8]; x3[3:0] = in_1[15:12]; x4[3:0] = in_1[19:16];
  //   x5[3:0] = in_1[23:20]; x6[3:0] = in_1[27:24]; x7[3:0] = in_1[31:28]; Y[31:0] = in_2; y0[3:0] = in_2[3:0];
  //   y1[3:0] = in_2[7:4]; y2[3:0] = in_2[11:8]; y3[3:0] = in_2[15:12]; y4[3:0] = in_2[19:16]; y5[3:0] = in_2[23:20];
  //   y6[3:0] = in_2[27:24]; y7[3:0] = in_2[31:28]

  // Notes on the sheet:
  //   输入引脚区
  //   计算部分
  //   输出引脚区
  //   有符号加法
  //   无符号加法
endmodule
