// Logisim project 海明编码.circ as structural Verilog: 4 circuits, main circuit 海明解码
module \海明解码  (
  input  [21:0] in_1,
  output out_2,
  output out_3,
  output out_4,
  output [15:0] out_5
);

  wire and_1_out, and_2_out, decoder_1_out3, decoder_1_out5, decoder_1_out6, decoder_1_out7, decoder_1_out9,
       decoder_1_out10, decoder_1_out11, decoder_1_out12, decoder_1_out13, decoder_1_out14, decoder_1_out15,
       decoder_1_out17, decoder_1_out18, decoder_1_out19, decoder_1_out20, decoder_1_out21, G1, G2, G3, G4,
       G5, G6, not_1_out, not_2_out, xor_17_out, xor_18_out, xor_19_out, xor_20_out, xor_21_out, xor_22_out,
       xor_23_out;

  Decoder #(.select(5)) decoder_1 (
    .out3(decoder_1_out3), .out5(decoder_1_out5), .out6(decoder_1_out6), .out7(decoder_1_out7),
    .out9(decoder_1_out9), .out10(decoder_1_out10), .out11(decoder_1_out11), .out12(decoder_1_out12),
    .out13(decoder_1_out13), .out14(decoder_1_out14), .out15(decoder_1_out15), .out17(decoder_1_out17),
    .out18(decoder_1_out18), .out19(decoder_1_out19), .out20(decoder_1_out20), .out21(decoder_1_out21),
    .sel({G5, G4, G3, G2, G1}), .en(1'b1));  // open: out0, out1, out2, out4, out8, out16, out22, out23, out24, out25, out26, out27, out28, out29, out30, out31
  xor xor_1 (out_5[4], decoder_1_out9, in_1[8]);
  xor xor_2 (out_5[3], decoder_1_out7, in_1[6]);
  xor xor_3 (out_5[2], decoder_1_out6, in_1[5]);
  xor xor_4 (out_5[1], decoder_1_out5, in_1[4]);
  xor xor_5 (out_5[0], decoder_1_out3, in_1[2]);
  xor xor_6 (out_5[11], decoder_1_out17, in_1[16]);
  xor xor_7 (out_5[10], decoder_1_out15, in_1[14]);
  xor xor_8 (out_5[9], decoder_1_out14, in_1[13]);
  xor xor_9 (out_5[8], decoder_1_out13, in_1[12]);
  xor xor_10 (out_5[7], decoder_1_out12, in_1[11]);
  xor xor_11 (out_5[6], decoder_1_out11, in_1[10]);
  xor xor_12 (out_5[5], decoder_1_out10, in_1[9]);
  xor xor_13 (out_5[15], decoder_1_out21, in_1[20]);
  xor xor_14 (out_5[14], decoder_1_out20, in_1[19]);
  xor xor_15 (out_5[13], decoder_1_out19, in_1[18]);
  xor xor_16 (out_5[12], decoder_1_out18, in_1[17]);
  xor xor_17 (xor_17_out, in_1[2], in_1[4], in_1[6], in_1[8], in_1[10], in_1[12], in_1[14], in_1[16], in_1[18], in_1[20]);
  xor xor_18 (xor_18_out, in_1[2], in_1[5], in_1[6], in_1[9], in_1[10], in_1[13], in_1[14], in_1[17], in_1[18]);
  xor xor_19 (xor_19_out, in_1[4], in_1[5], in_1[6], in_1[11], in_1[12], in_1[13], in_1[14], in_1[19], in_1[20]);
  xor xor_20 (xor_20_out, in_1[8], in_1[9], in_1[10], in_1[11], in_1[12], in_1[13], in_1[14]);
  xor xor_21 (xor_21_out, in_1[16], in_1[17], in_1[18], in_1[19], in_1[20]);
  xor xor_22 (xor_22_out, G1, G2, G3, G4, G5);
  not not_1 (not_1_out, xor_22_out);
  xor xor_23 (xor_23_out, in_1[20], in_1[19], in_1[18], in_1[17], in_1[16], in_1[14], in_1[13], in_1[12], in_1[11], in_1[10], xor_21_out, in_1[9], in_1[8], in_1[6], in_1[5], in_1[4], in_1[2], xor_20_out, xor_19_out, xor_18_out, xor_17_out);
  xor xor_24 (G1, xor_17_out, in_1[0]);
  xor xor_25 (G2, xor_18_out, in_1[1]);
  xor xor_26 (G3, xor_19_out, in_1[3]);
  xor xor_27 (G4, xor_20_out, in_1[7]);
  xor xor_28 (G5, xor_21_out, in_1[15]);
  and and_1 (and_1_out, xor_22_out, G6);
  and and_2 (and_2_out, not_1_out, G6);
  not not_2 (not_2_out, G6);
  xor xor_29 (G6, xor_23_out, in_1[21]);
  or or_1 (out_3, and_1_out, and_2_out);
  and and_3 (out_4, xor_22_out, not_2_out);
  and and_4 (out_2, not_1_out, not_2_out);

  // Other names for the same wires on the sheet: _1位错 = out_3; _2位错 = out_4; 无错误 = out_2; P1 = in_1[0];
  //   海明码[21:0] = in_1; P2 = in_1[1]; D1 = in_1[2]; P3 = in_1[3]; D2 = in_1[4]; D3 = in_1[5]; D4 = in_1[6];
  //   P4 = in_1[7]; D5 = in_1[8]; D6 = in_1[9]; D7 = in_1[10]; D8 = in_1[11]; D9 = in_1[12]; D10 = in_1[13];
  //   D11 = in_1[14]; P5 = in_1[15]; D12 = in_1[16]; D13 = in_1[17]; D14 = in_1[18]; D15 = in_1[19]; D16 = in_1[20];
  //   P6 = in_1[21]; 纠错后数据[15:0] = out_5

  // Notes on the sheet:
  //   输出引脚区
  //   海明码
  //   输入引脚区
  //   改错
  //   数据处理区
  //   判断错误位数
endmodule

module \海明编码  (
  input  [15:0] in_1,
  output [21:0] out_2
);

  xor xor_1 (out_2[0], in_1[0], in_1[1], in_1[3], in_1[4], in_1[6], in_1[8], in_1[10], in_1[11], in_1[13], in_1[15]);
  xor xor_2 (out_2[1], in_1[0], in_1[2], in_1[3], in_1[5], in_1[6], in_1[9], in_1[10], in_1[12], in_1[13]);
  xor xor_3 (out_2[3], in_1[1], in_1[2], in_1[3], in_1[7], in_1[8], in_1[9], in_1[10], in_1[14], in_1[15]);
  xor xor_4 (out_2[7], in_1[4], in_1[5], in_1[6], in_1[7], in_1[8], in_1[9], in_1[10]);
  xor xor_5 (out_2[15], in_1[11], in_1[12], in_1[13], in_1[14], in_1[15]);
  xor xor_6 (out_2[21], in_1[15], in_1[14], in_1[13], in_1[12], in_1[11], in_1[10], in_1[9], in_1[8], in_1[7], in_1[6], out_2[15], in_1[5], in_1[4], in_1[3], in_1[2], in_1[1], in_1[0], out_2[7], out_2[3], out_2[1], out_2[0]);

  assign {out_2[20:16], out_2[14:8], out_2[6:4], out_2[2]} = in_1;

  // Other names for the same wires on the sheet: P1 = out_2[0];
  //   海明码[21:0] = {out_2[21], in_1[15:11], out_2[15], in_1[10:4], out_2[7], in_1[3:1], out_2[3], in_1[0], out_2[1:0]};
  //   P2 = out_2[1]; D1 = in_1[0]; Data[15:0] = in_1; P3 = out_2[3]; D2 = in_1[1]; D3 = in_1[2]; D4 = in_1[3];
  //   P4 = out_2[7]; D5 = in_1[4]; D6 = in_1[5]; D7 = in_1[6]; D8 = in_1[7]; D9 = in_1[8]; D10 = in_1[9];
  //   D11 = in_1[10]; P5 = out_2[15]; D12 = in_1[11]; D13 = in_1[12]; D14 = in_1[13]; D15 = in_1[14]; D16 = in_1[15];
  //   P6 = out_2[21]

  // Notes on the sheet:
  //   求校验位
  //   输入引脚区
  //   原始数据（16位）
  //   整合海明码
  //   海明码（22位）
  //   输出引脚区
endmodule

module main (
  input  [15:0] in_1,
  input  [1:0] \加扰控制 ,
  output [21:0] \干扰后校验码 ,
  output [21:0] \_22位校验码 ,
  output [15:0] \改错后数据 
);

  wire comparator_1_eq, \时钟_out , \解码部分_out_2 , \解码部分_out_3 , \解码部分_out_4 ;

  // Probe on in_1
  // Probe on \_22位校验码 
  \海明编码  \u_编码部分  (.in_1(in_1), .out_2(\_22位校验码 ));
  Clock \u_时钟  (.out(\时钟_out ));
  \随机干扰  \u_随机干扰_1  (
    .CLK(\时钟_out ), .\_22位输入 (\_22位校验码 ), .\加扰模式 (\加扰控制 ), .\加扰后数据 (\干扰后校验码 ));  // open: 增加三位错, 随机加扰屏蔽字, EDU
  \海明解码  \u_解码部分  (.out_2(\解码部分_out_2 ), .out_3(\解码部分_out_3 ), .out_4(\解码部分_out_4 ), .out_5(\改错后数据 ), .in_1(\干扰后校验码 ));
  // Probe on \改错后数据 
  Comparator #(.width(16)) comparator_1 (.a(in_1), .b(\改错后数据 ), .eq(comparator_1_eq));  // open: gt, lt
  LED led_1 (.in(comparator_1_eq));
  LED led_2 (.in(\解码部分_out_4 ));
  LED led_3 (.in(\解码部分_out_3 ));
  LED led_4 (.in(\解码部分_out_2 ));

  // Notes on the sheet:
  //   原始数据
  //   时钟必须先点开，否则结果错误
  //   灯亮表示正确传输
  //   灯亮表示1个错
  //   灯亮表示2个错
  //   灯亮表示无错
endmodule

// 随机干扰部分
module \随机干扰  (
  input  CLK,
  input  [21:0] \_22位输入 ,
  input  EDU,
  input  [1:0] \加扰模式 ,
  input  \增加三位错 ,
  output [21:0] \随机加扰屏蔽字 ,
  output [21:0] \加扰后数据 
);

  wire comparator_1_eq, \随机信号_5_out ;
  wire [1:0] EDUerr, multiplexer_3_out, \随机信号_4_out ;
  wire [3:0] \随机信号_2_out , \随机信号_3_out , \随机信号_out ;
  wire [7:0] counter_1_q;
  wire [15:0] \_1位加扰A ;
  wire [21:0] \_1位加扰 , \_1位加扰A_t , \_1位加扰B_t , \_2位加扰 , \_3位加扰 , multiplexer_1_out, multiplexer_5_out,
       shifter_1_out, \随机加扰 ;
  wire [21:6] \_1位加扰B , \_1位加扰C ;

  Decoder #(.select(4), .enable("false")) decoder_1 (
    .out0(\_1位加扰A [0]), .out1(\_1位加扰A [1]), .out2(\_1位加扰A [2]), .out3(\_1位加扰A [3]), .out4(\_1位加扰A [4]),
    .out5(\_1位加扰A [5]), .out6(\_1位加扰A [6]), .out7(\_1位加扰A [7]), .out8(\_1位加扰A [8]), .out9(\_1位加扰A [9]),
    .out10(\_1位加扰A [10]), .out11(\_1位加扰A [11]), .out12(\_1位加扰A [12]), .out13(\_1位加扰A [13]),
    .out14(\_1位加扰A [14]), .out15(\_1位加扰A [15]), .sel(\随机信号_out ));
  Random #(.width(4)) \u_随机信号  (.clk(CLK), .out(\随机信号_out ));  // open: next, clr
  Decoder #(.select(4), .enable("false")) decoder_2 (
    .out0(\_1位加扰B [6]), .out1(\_1位加扰B [7]), .out2(\_1位加扰B [8]), .out3(\_1位加扰B [9]), .out4(\_1位加扰B [10]),
    .out5(\_1位加扰B [11]), .out6(\_1位加扰B [12]), .out7(\_1位加扰B [13]), .out8(\_1位加扰B [14]), .out9(\_1位加扰B [15]),
    .out10(\_1位加扰B [16]), .out11(\_1位加扰B [17]), .out12(\_1位加扰B [18]), .out13(\_1位加扰B [19]),
    .out14(\_1位加扰B [20]), .out15(\_1位加扰B [21]), .sel(\随机信号_2_out ));
  Random #(.width(4), .seed(18)) \u_随机信号_2  (.clk(CLK), .out(\随机信号_2_out ));  // open: next, clr
  Random #(.width(4), .seed(3)) \u_随机信号_3  (.clk(CLK), .out(\随机信号_3_out ));  // open: next, clr
  Random #(.width(2), .seed(21)) \u_随机信号_4  (.clk(CLK), .out(\随机信号_4_out ));  // open: next, clr
  Random #(.width(1), .seed(31)) \u_随机信号_5  (.clk(CLK), .out(\随机信号_5_out ));  // open: next, clr
  Pull_Resistor #(.pull(1)) pull_resistor_1 (.node(\加扰模式 ));
  Decoder #(.select(4), .enable("false")) decoder_3 (
    .out0(\_1位加扰C [6]), .out1(\_1位加扰C [7]), .out2(\_1位加扰C [8]), .out3(\_1位加扰C [9]), .out4(\_1位加扰C [10]),
    .out5(\_1位加扰C [11]), .out6(\_1位加扰C [12]), .out7(\_1位加扰C [13]), .out8(\_1位加扰C [14]), .out9(\_1位加扰C [15]),
    .out10(\_1位加扰C [16]), .out11(\_1位加扰C [17]), .out12(\_1位加扰C [18]), .out13(\_1位加扰C [19]),
    .out14(\_1位加扰C [20]), .out15(\_1位加扰C [21]), .sel(\随机信号_3_out ));
  Pull_Resistor pull_resistor_2 (.node(\增加三位错 ));
  Multiplexer #(.width(22), .enable("false")) multiplexer_1 (
    .in0(\_1位加扰B_t ), .in1(\_3位加扰 ), .out(multiplexer_1_out), .sel(\增加三位错 ));
  Multiplexer #(.select(2), .width(22), .enable("false")) multiplexer_2 (
    .in0({22{1'b0}}), .in1(\_1位加扰A_t ), .in2(\_2位加扰 ), .in3(multiplexer_1_out), .out(\随机加扰 ),
    .sel(\随机信号_4_out ));
  Pull_Resistor pull_resistor_3 (.node(EDU));
  Multiplexer #(.width(2), .enable("false")) multiplexer_3 (
    .in0(\加扰模式 ), .in1(EDUerr), .out(multiplexer_3_out), .sel(EDU));
  Multiplexer #(.select(2), .width(22), .enable("false")) multiplexer_4 (
    .in0({22{1'b0}}), .in1(\_1位加扰 ), .in2(\_2位加扰 ), .in3(\随机加扰 ), .out(\随机加扰屏蔽字 ), .sel(multiplexer_3_out));
  Shifter #(.width(22), .shift("rl")) shifter_1 (.in({{6{1'b0}}, \_1位加扰A }), .\dist (5'b00001), .out(shifter_1_out));
  Comparator #(.width(22), .mode("unsigned")) comparator_1 (
    .a({{6{1'b0}}, \_1位加扰A }), .b({\_1位加扰B , {6{1'b0}}}), .eq(comparator_1_eq));  // open: gt, lt
  Counter counter_1 (.Q(counter_1_q), .clk(CLK));  // open: load, D, count, carry, clr
  Multiplexer #(.width(22), .enable("false")) multiplexer_5 (
    .in0({{6{1'b0}}, \_1位加扰A }), .in1(shifter_1_out), .out(multiplexer_5_out), .sel(comparator_1_eq));
  assign \_2位加扰  = multiplexer_5_out ^ {\_1位加扰B , {6{1'b0}}};  // XOR_Gate xor_1, 22 bits wide
  ROM #(.dataWidth(2)) rom_1 (.addr(counter_1_q), .data(EDUerr));  // open: sel
  assign \_3位加扰  = \_2位加扰  ^ {\_1位加扰C , {6{1'b0}}};  // XOR_Gate xor_2, 22 bits wide
  assign \加扰后数据  = \随机加扰屏蔽字  ^ \_22位输入 ;  // XOR_Gate xor_3, 22 bits wide
  Multiplexer #(.width(22), .enable("false")) multiplexer_6 (
    .in0(multiplexer_5_out), .in1({\_1位加扰B , {6{1'b0}}}), .out(\_1位加扰 ), .sel(\随机信号_5_out ));
endmodule
